// Logisim project ULA4_semana01.circ as structural Verilog: 1 circuit, main circuit main
module main (
  input  C,
  input  [3:0] A,
  input  [3:0] B,
  input  V,
  input  [2:0] OP,
  input  Z,
  output [7:0] F
);


  assign B = A;

  // Notes on the sheet:
  //   ULA4
endmodule
